// Logisim project CPU.circ as structural Verilog: 10 circuits, main circuit main
module main (
  input  reset,
  output [31:0] out_2,
  output [31:0] out_3,
  output out_4,
  output [4:0] out_5,
  output [31:0] out_6,
  output out_7,
  output [31:0] out_8,
  output [31:0] out_9
);

  wire alu_1_out_6, ALUINsel, and_1_out, and_2_out, clock_1_out, IMchoose, NPCsel, or_1_out, zeroSign;
  wire [1:0] ALUop, EXTop, WriteBackOp;
  wire [1:1] memOp;
  wire [4:0] break_1_rs, break_1_rt;
  wire [5:0] break_1_function, break_1_opcode;
  wire [15:0] break_1_imm;
  wire [31:0] dm_1_wb, ext_1_out_3, grf_1_out_8, multiplexer_1_out, NPC_out_4, PC;

  Clock clock_1 (.out(clock_1_out));
  and and_1 (and_1_out, NPCsel, zeroSign);
  and and_2 (and_2_out, NPCsel, alu_1_out_6);
  or or_1 (or_1_out, and_1_out, and_2_out);
  PC u_PC (.in_3(NPC_out_4), .clk(clock_1_out), .in_2(reset), .out_4(PC));
  NPC NPC (.in_2(PC), .imm(ext_1_out_3), .NPCco(or_1_out), .out_4(NPC_out_4));
  IM im_1 (.in_1(PC), .out_2(out_2));
  Control control_1 (
    .opcode(break_1_opcode), .func(break_1_function), .out_3(ALUop), .out_4(EXTop), .out_5(NPCsel),
    .out_6(out_4), .out_7(ALUINsel), .out_8(WriteBackOp), .out_9({memOp[1], out_7}), .out_10(IMchoose));
  \break  break_1 (
    .in_2(out_2), .IMchoose(IMchoose), .\function (break_1_function), .rs(break_1_rs), .rt(break_1_rt),
    .rd(out_5), .opcode(break_1_opcode), .imm(break_1_imm));
  GRF grf_1 (
    .rs(break_1_rs), .rt(break_1_rt), .rd(out_5), .WB(out_6), .clk(clock_1_out), .reset(reset), .WE(out_4),
    .out_8(grf_1_out_8), .out_9(out_9));
  // Probe on out_6
  EXT ext_1 (.in_2(break_1_imm), .out_3(ext_1_out_3), .EXTop(EXTop));
  Multiplexer #(.width(32)) multiplexer_1 (
    .in0(out_9), .in1(ext_1_out_3), .out(multiplexer_1_out), .sel(ALUINsel));  // open: en
  ALU alu_1 (
    .in_2(grf_1_out_8), .in_3(multiplexer_1_out), .out_5(out_8), .ALUop(ALUop), .zero(zeroSign),
    .out_6(alu_1_out_6));
  DM dm_1 (.Address(out_8), .DATA(out_9), .memWrite({memOp[1], out_7}), .clk(clock_1_out), .reset(reset), .WB(dm_1_wb));
  Multiplexer #(.select(2), .width(32)) multiplexer_2 (
    .in0(out_8), .in1(dm_1_wb), .in2(ext_1_out_3), .out(out_6), .sel(WriteBackOp));  // open: in3, en
  Adder #(.width(32)) adder_1 (.a(PC), .b(32'h3000), .out(out_3));  // open: cin, cout

  // Other names for the same wires on the sheet: GRFop = out_4; Instr[31:0] = out_2; MemAddr[31:0] = out_8;
  //   MemData[31:0] = out_9; memOp[0] = out_7; RegAddr[4:0] = out_5; RegData[31:0] = out_6
endmodule

module GRF (
  input  clk,
  input  reset,
  input  WE,
  input  [4:0] rs,
  input  [4:0] rt,
  input  [4:0] rd,
  input  [31:0] WB,
  output [31:0] out_8,
  output [31:0] out_9
);

  wire [31:0] demultiplexer_1_out1, demultiplexer_1_out2, demultiplexer_1_out3, demultiplexer_1_out4,
       demultiplexer_1_out5, demultiplexer_1_out6, demultiplexer_1_out7, demultiplexer_1_out8,
       demultiplexer_1_out9, demultiplexer_1_out10, demultiplexer_1_out11, demultiplexer_1_out12,
       demultiplexer_1_out13, demultiplexer_1_out14, demultiplexer_1_out15, demultiplexer_1_out16,
       demultiplexer_1_out17, demultiplexer_1_out18, demultiplexer_1_out19, demultiplexer_1_out20,
       demultiplexer_1_out21, demultiplexer_1_out22, demultiplexer_1_out23, demultiplexer_1_out24,
       demultiplexer_1_out25, demultiplexer_1_out26, demultiplexer_1_out27, demultiplexer_1_out28,
       demultiplexer_1_out29, demultiplexer_1_out30, demultiplexer_1_out31, register_1_q, register_2_q,
       register_3_q, register_4_q, register_5_q, register_6_q, register_7_q, register_8_q, register_9_q,
       register_10_q, register_11_q, register_12_q, register_13_q, register_14_q, register_15_q,
       register_16_q, register_17_q, register_18_q, register_19_q, register_20_q, register_21_q,
       register_22_q, register_23_q, register_24_q, register_25_q, register_26_q, register_27_q,
       register_28_q, register_29_q, register_30_q, register_31_q;

  Demultiplexer #(.select(5), .width(32), .tristate("true")) demultiplexer_1 (
    .out1(demultiplexer_1_out1), .out2(demultiplexer_1_out2), .out3(demultiplexer_1_out3),
    .out4(demultiplexer_1_out4), .out5(demultiplexer_1_out5), .out6(demultiplexer_1_out6),
    .out7(demultiplexer_1_out7), .out8(demultiplexer_1_out8), .out9(demultiplexer_1_out9),
    .out10(demultiplexer_1_out10), .out11(demultiplexer_1_out11), .out12(demultiplexer_1_out12),
    .out13(demultiplexer_1_out13), .out14(demultiplexer_1_out14), .out15(demultiplexer_1_out15),
    .out16(demultiplexer_1_out16), .out17(demultiplexer_1_out17), .out18(demultiplexer_1_out18),
    .out19(demultiplexer_1_out19), .out20(demultiplexer_1_out20), .out21(demultiplexer_1_out21),
    .out22(demultiplexer_1_out22), .out23(demultiplexer_1_out23), .out24(demultiplexer_1_out24),
    .out25(demultiplexer_1_out25), .out26(demultiplexer_1_out26), .out27(demultiplexer_1_out27),
    .out28(demultiplexer_1_out28), .out29(demultiplexer_1_out29), .out30(demultiplexer_1_out30),
    .out31(demultiplexer_1_out31), .in(WB), .sel(rd));  // open: out0, en
  Register #(.width(32)) register_1 (.D(demultiplexer_1_out8), .en(WE), .Q(register_1_q), .clk(clk), .clr(reset));
  Register #(.width(32)) register_2 (.D(demultiplexer_1_out16), .en(WE), .Q(register_2_q), .clk(clk), .clr(reset));
  Register #(.width(32)) register_3 (.D(demultiplexer_1_out24), .en(WE), .Q(register_3_q), .clk(clk), .clr(reset));
  Register #(.width(32)) register_4 (.D(demultiplexer_1_out1), .en(WE), .Q(register_4_q), .clk(clk), .clr(reset));
  Register #(.width(32)) register_5 (.D(demultiplexer_1_out9), .en(WE), .Q(register_5_q), .clk(clk), .clr(reset));
  Register #(.width(32)) register_6 (.D(demultiplexer_1_out17), .en(WE), .Q(register_6_q), .clk(clk), .clr(reset));
  Register #(.width(32)) register_7 (.D(demultiplexer_1_out25), .en(WE), .Q(register_7_q), .clk(clk), .clr(reset));
  Register #(.width(32)) register_8 (.D(demultiplexer_1_out2), .en(WE), .Q(register_8_q), .clk(clk), .clr(reset));
  Register #(.width(32)) register_9 (.D(demultiplexer_1_out10), .en(WE), .Q(register_9_q), .clk(clk), .clr(reset));
  Register #(.width(32)) register_10 (.D(demultiplexer_1_out18), .en(WE), .Q(register_10_q), .clk(clk), .clr(reset));
  Register #(.width(32)) register_11 (.D(demultiplexer_1_out26), .en(WE), .Q(register_11_q), .clk(clk), .clr(reset));
  Register #(.width(32)) register_12 (.D(demultiplexer_1_out3), .en(WE), .Q(register_12_q), .clk(clk), .clr(reset));
  Register #(.width(32)) register_13 (.D(demultiplexer_1_out11), .en(WE), .Q(register_13_q), .clk(clk), .clr(reset));
  Register #(.width(32)) register_14 (.D(demultiplexer_1_out19), .en(WE), .Q(register_14_q), .clk(clk), .clr(reset));
  Register #(.width(32)) register_15 (.D(demultiplexer_1_out27), .en(WE), .Q(register_15_q), .clk(clk), .clr(reset));
  Register #(.width(32)) register_16 (.D(demultiplexer_1_out4), .en(WE), .Q(register_16_q), .clk(clk), .clr(reset));
  Register #(.width(32)) register_17 (.D(demultiplexer_1_out12), .en(WE), .Q(register_17_q), .clk(clk), .clr(reset));
  Register #(.width(32)) register_18 (.D(demultiplexer_1_out20), .en(WE), .Q(register_18_q), .clk(clk), .clr(reset));
  Register #(.width(32)) register_19 (.D(demultiplexer_1_out28), .en(WE), .Q(register_19_q), .clk(clk), .clr(reset));
  Register #(.width(32)) register_20 (.D(demultiplexer_1_out5), .en(WE), .Q(register_20_q), .clk(clk), .clr(reset));
  Register #(.width(32)) register_21 (.D(demultiplexer_1_out13), .en(WE), .Q(register_21_q), .clk(clk), .clr(reset));
  Register #(.width(32)) register_22 (.D(demultiplexer_1_out21), .en(WE), .Q(register_22_q), .clk(clk), .clr(reset));
  Register #(.width(32)) register_23 (.D(demultiplexer_1_out29), .en(WE), .Q(register_23_q), .clk(clk), .clr(reset));
  Register #(.width(32)) register_24 (.D(demultiplexer_1_out6), .en(WE), .Q(register_24_q), .clk(clk), .clr(reset));
  Register #(.width(32)) register_25 (.D(demultiplexer_1_out14), .en(WE), .Q(register_25_q), .clk(clk), .clr(reset));
  Register #(.width(32)) register_26 (.D(demultiplexer_1_out22), .en(WE), .Q(register_26_q), .clk(clk), .clr(reset));
  Register #(.width(32)) register_27 (.D(demultiplexer_1_out30), .en(WE), .Q(register_27_q), .clk(clk), .clr(reset));
  Register #(.width(32)) register_28 (.D(demultiplexer_1_out7), .en(WE), .Q(register_28_q), .clk(clk), .clr(reset));
  Register #(.width(32)) register_29 (.D(demultiplexer_1_out15), .en(WE), .Q(register_29_q), .clk(clk), .clr(reset));
  Register #(.width(32)) register_30 (.D(demultiplexer_1_out23), .en(WE), .Q(register_30_q), .clk(clk), .clr(reset));
  Register #(.width(32)) register_31 (.D(demultiplexer_1_out31), .en(WE), .Q(register_31_q), .clk(clk), .clr(reset));
  Multiplexer #(.select(5), .width(32)) multiplexer_1 (
    .in0({32{1'b0}}), .in1(register_4_q), .in2(register_8_q), .in3(register_12_q), .in4(register_16_q),
    .in5(register_20_q), .in6(register_24_q), .in7(register_28_q), .in8(register_1_q), .in9(register_5_q),
    .in10(register_9_q), .in11(register_13_q), .in12(register_17_q), .in13(register_21_q),
    .in14(register_25_q), .in15(register_29_q), .in16(register_2_q), .in17(register_6_q),
    .in18(register_10_q), .in19(register_14_q), .in20(register_18_q), .in21(register_22_q),
    .in22(register_26_q), .in23(register_30_q), .in24(register_3_q), .in25(register_7_q),
    .in26(register_11_q), .in27(register_15_q), .in28(register_19_q), .in29(register_23_q),
    .in30(register_27_q), .in31(register_31_q), .out(out_8), .sel(rs));  // open: en
  Multiplexer #(.select(5), .width(32)) multiplexer_2 (
    .in0({32{1'b0}}), .in1(register_4_q), .in2(register_8_q), .in3(register_12_q), .in4(register_16_q),
    .in5(register_20_q), .in6(register_24_q), .in7(register_28_q), .in8(register_1_q), .in9(register_5_q),
    .in10(register_9_q), .in11(register_13_q), .in12(register_17_q), .in13(register_21_q),
    .in14(register_25_q), .in15(register_29_q), .in16(register_2_q), .in17(register_6_q),
    .in18(register_10_q), .in19(register_14_q), .in20(register_18_q), .in21(register_22_q),
    .in22(register_26_q), .in23(register_30_q), .in24(register_3_q), .in25(register_7_q),
    .in26(register_11_q), .in27(register_15_q), .in28(register_19_q), .in29(register_23_q),
    .in30(register_27_q), .in31(register_31_q), .out(out_9), .sel(rt));  // open: en
endmodule

module ALU (
  input  [1:0] ALUop,
  input  [31:0] in_2,
  input  [31:0] in_3,
  output zero,
  output [31:0] out_5,
  output out_6
);

  wire even_parity_1_out, odd_parity_1_out;
  wire [31:0] adder_1_out, or_1_out, subtractor_1_out;

  Comparator #(.width(32), .mode("unsigned")) comparator_1 (.a(in_2), .b(in_3), .eq(zero));  // open: gt, lt
  Adder #(.width(32)) adder_1 (.a(in_2), .b(in_3), .out(adder_1_out));  // open: cin, cout
  Subtractor #(.width(32)) subtractor_1 (.a(in_2), .b(in_3), .out(subtractor_1_out));  // open: bin, bout
  assign or_1_out = in_2 | in_3;  // OR_Gate or_1, 32 bits wide
  // Probe on or_1_out
  Multiplexer #(.select(2), .width(32)) multiplexer_1 (
    .in0({32{1'b0}}), .in1(adder_1_out), .in2(subtractor_1_out), .in3(or_1_out), .out(out_5), .sel(ALUop));  // open: en
  xor odd_parity_1 (odd_parity_1_out, in_2[0], in_2[1], in_2[2], in_2[3], in_2[4], in_2[5], in_2[6], in_2[7], in_2[8], in_2[9], in_2[10], in_2[11], in_2[12], in_2[13], in_2[14], in_2[15]);
  xnor even_parity_1 (even_parity_1_out, in_3[16], in_3[17], in_3[18], in_3[19], in_3[20], in_3[21], in_3[22], in_3[23], in_3[24], in_3[25], in_3[26], in_3[27], in_3[28], in_3[29], in_3[30], in_3[31]);
  and and_1 (out_6, odd_parity_1_out, even_parity_1_out);
endmodule

module EXT (
  input  [1:0] EXTop,
  input  [15:0] in_2,
  output [31:0] out_3
);

  wire [31:0] bit_extender_1_out, bit_extender_2_out;

  assign bit_extender_1_out = {{16{in_2[15]}}, in_2};  // Bit_Extender bit_extender_1
  assign bit_extender_2_out = {{16{1'b0}}, in_2};  // Bit_Extender bit_extender_2
  Multiplexer #(.select(2), .width(32)) multiplexer_1 (
    .in0({32{1'b0}}), .in1(bit_extender_2_out), .in2(bit_extender_1_out), .in3({in_2, {16{1'b0}}}),
    .out(out_3), .sel(EXTop));  // open: en
endmodule

module PC (
  input  clk,
  input  in_2,
  input  [31:0] in_3,
  output [31:0] out_4
);

  Register #(.width(32)) register_1 (.D(in_3), .Q(out_4), .clk(clk), .clr(in_2));  // open: en
endmodule

module IM (
  input  [31:0] in_1,
  output [31:0] out_2
);

  ROM #(.addrWidth(12), .dataWidth(32)) rom_1 (.addr(in_1[13:2]), .data(out_2));  // open: sel

  // Notes on the sheet:
  //   contents of rom_1 (hex, n*v repeats v):
  //   3529ea60 ac090004 ac090c00 8c0a0c00
endmodule

module NPC (
  input  NPCco,
  input  [31:0] in_2,
  input  [31:0] imm,
  output [31:0] out_4
);

  wire [31:0] adder_1_out, adder_2_out;

  Adder #(.width(32)) adder_1 (.a(in_2), .b(32'h4), .out(adder_1_out));  // open: cin, cout
  Adder #(.width(32)) adder_2 (.a(adder_1_out), .b({imm[29:0], 2'b00}), .out(adder_2_out));  // open: cin, cout
  Multiplexer #(.width(32)) multiplexer_1 (.in0(adder_1_out), .in1(adder_2_out), .out(out_4), .sel(NPCco));  // open: en
endmodule

module Control (
  input  [5:0] opcode,
  input  [5:0] func,
  output [1:0] out_3,
  output [1:0] out_4,
  output out_5,
  output out_6,
  output out_7,
  output [1:0] out_8,
  output [1:0] out_9,
  output out_10
);

  wire add_out, beq_out, lui_out, lw_out, not_1_out, not_2_out, not_3_out, not_4_out, not_5_out, not_6_out,
       not_7_out, not_8_out, not_9_out, not_10_out, not_11_out, not_12_out, ori_out, sub_out, sw_out;

  not not_1 (not_1_out, func[0]);
  not not_2 (not_2_out, func[2]);
  not not_3 (not_3_out, func[1]);
  not not_4 (not_4_out, func[3]);
  not not_5 (not_5_out, func[4]);
  not not_6 (not_6_out, func[5]);
  not not_7 (not_7_out, opcode[0]);
  not not_8 (not_8_out, opcode[1]);
  not not_9 (not_9_out, opcode[2]);
  not not_10 (not_10_out, opcode[4]);
  not not_11 (not_11_out, opcode[3]);
  not not_12 (not_12_out, opcode[5]);
  and add (add_out, not_12_out, not_10_out, not_11_out, not_9_out, not_8_out, not_7_out, func[5], not_5_out, not_4_out, not_2_out, not_3_out, not_1_out);
  and sub (sub_out, not_12_out, not_10_out, not_11_out, not_9_out, not_8_out, not_7_out, func[5], not_5_out, not_4_out, not_2_out, func[1], not_1_out);
  and ori (ori_out, not_12_out, not_10_out, opcode[3], opcode[2], not_8_out, opcode[0]);
  and lw (lw_out, opcode[5], not_10_out, not_11_out, not_9_out, opcode[1], opcode[0]);
  and sw (sw_out, opcode[5], not_10_out, opcode[3], not_9_out, opcode[1], opcode[0]);
  and beq (beq_out, not_12_out, not_10_out, not_11_out, opcode[2], not_8_out, not_7_out);
  and lui (lui_out, not_12_out, not_10_out, opcode[3], opcode[2], opcode[1], opcode[0]);
  or ALU1 (out_3[1], sub_out, ori_out);
  or ALU2 (out_3[0], add_out, ori_out, lw_out, sw_out);
  or EXT1_prime (out_4[1], lw_out, sw_out, beq_out, lui_out);
  or EXT2 (out_4[0], ori_out, lui_out);
  buf NPCsel (out_5, beq_out);  // OR_Gate
  or GRFop (out_6, add_out, sub_out, ori_out, lw_out, lui_out);
  or ALUINsel (out_7, ori_out, lw_out, sw_out);
  buf WBop (out_8[1], lui_out);  // OR_Gate
  buf WBop2 (out_8[0], lw_out);  // OR_Gate
  buf memop (out_9[1], lw_out);  // OR_Gate
  buf memop2 (out_9[0], sw_out);  // OR_Gate
  or IMchoose (out_10, ori_out, lw_out, sw_out, lui_out);

  // Other names for the same wires on the sheet: func5 = func[0]; func4 = func[1]; func3 = func[2]; func2 = func[3];
  //   func1 = func[4]; func0 = func[5]; op5 = opcode[0]; op4 = opcode[1]; op3 = opcode[2]; op2 = opcode[3];
  //   op1 = opcode[4]; op0 = opcode[5]
endmodule

module \break  (
  input  IMchoose,
  input  [31:0] in_2,
  output [5:0] \function ,
  output [4:0] rs,
  output [4:0] rt,
  output [4:0] rd,
  output [5:0] opcode,
  output [15:0] imm
);

  Multiplexer #(.width(5)) multiplexer_1 (.in0(in_2[15:11]), .in1(in_2[20:16]), .out(rd), .sel(IMchoose));  // open: en

  assign \function  = in_2[5:0];
  assign imm = in_2[15:0];
  assign opcode = in_2[31:26];
  assign rs = in_2[25:21];
  assign rt = in_2[20:16];
endmodule

module DM (
  input  [1:0] memWrite,
  input  clk,
  input  reset,
  input  [31:0] Address,
  input  [31:0] DATA,
  output [31:0] WB
);

  wire demultiplexer_1_out1, demultiplexer_1_out2;

  Demultiplexer #(.select(2)) demultiplexer_1 (
    .out1(demultiplexer_1_out1), .out2(demultiplexer_1_out2), .in(1'b1), .sel(memWrite));  // open: out0, out3, en
  RAM #(.addrWidth(12), .dataWidth(32), .bus("separate")) ram_1 (
    .addr(Address[13:2]), .din(DATA), .data(WB), .str(demultiplexer_1_out1), .clk(clk),
    .ld(demultiplexer_1_out2), .clr(reset));  // open: sel
endmodule
