// Logisim project CRC.circ as structural Verilog: 3 circuits, main circuit CRC
module CRC (
  input  [7:0] in_1,
  input  [3:0] in_2,
  output [10:0] out_3
);

  wire [3:0] n4nit_1_out_3, n4nit_2_out_3, n4nit_3_out_3, n4nit_4_out_3, n4nit_5_out_3, n4nit_6_out_3,
       n4nit_7_out_3, right_1_out_3, right_2_out_3, right_3_out_3, right_4_out_3, right_5_out_3,
       right_6_out_3, right_7_out_3;
  wire [3:3] n4nit_8_out_3;

  _4nit u_4nit_1 (.in_1(in_1[7:4]), .in_2(in_2), .out_3(n4nit_1_out_3));  // open: out_4
  right right_1 (.in_1(in_1[3]), .in_2(n4nit_1_out_3), .out_3(right_1_out_3));
  _4nit u_4nit_2 (.in_1(right_1_out_3), .in_2(in_2), .out_3(n4nit_2_out_3));  // open: out_4
  right right_2 (.in_1(in_1[2]), .in_2(n4nit_2_out_3), .out_3(right_2_out_3));
  _4nit u_4nit_3 (.in_1(right_2_out_3), .in_2(in_2), .out_3(n4nit_3_out_3));  // open: out_4
  right right_3 (.in_1(in_1[1]), .in_2(n4nit_3_out_3), .out_3(right_3_out_3));
  _4nit u_4nit_4 (.in_1(right_3_out_3), .in_2(in_2), .out_3(n4nit_4_out_3));  // open: out_4
  right right_4 (.in_1(in_1[0]), .in_2(n4nit_4_out_3), .out_3(right_4_out_3));
  _4nit u_4nit_5 (.in_1(right_4_out_3), .in_2(in_2), .out_3(n4nit_5_out_3));  // open: out_4
  right right_5 (.in_1(1'b0), .in_2(n4nit_5_out_3), .out_3(right_5_out_3));
  _4nit u_4nit_6 (.in_1(right_5_out_3), .in_2(in_2), .out_3(n4nit_6_out_3));  // open: out_4
  right right_6 (.in_1(1'b0), .in_2(n4nit_6_out_3), .out_3(right_6_out_3));
  _4nit u_4nit_7 (.in_1(right_6_out_3), .in_2(in_2), .out_3(n4nit_7_out_3));  // open: out_4
  right right_7 (.in_1(1'b0), .in_2(n4nit_7_out_3), .out_3(right_7_out_3));
  _4nit u_4nit_8 (.in_1(right_7_out_3), .in_2(in_2), .out_3({n4nit_8_out_3[3], out_3[2:0]}));  // open: out_4

  assign out_3[10:3] = in_1;
endmodule

module _4nit (
  input  [3:0] in_1,
  input  [3:0] in_2,
  output [3:0] out_3,
  output out_4
);

  wire [3:0] xor_1_out;

  assign xor_1_out = in_1 ^ in_2;  // XOR_Gate xor_1, 4 bits wide
  Multiplexer #(.width(4)) multiplexer_1 (.in0(in_1), .in1(xor_1_out), .out(out_3), .sel(in_1[3]));  // open: en
  Multiplexer multiplexer_2 (.in0(1'b0), .in1(1'b1), .out(out_4), .sel(in_1[3]));  // open: en
endmodule

module right (
  input  in_1,
  input  [3:0] in_2,
  output [3:0] out_3
);


  assign out_3 = {in_2[2:0], in_1};
endmodule
