// Logisim project FSMver2.0.circ as structural Verilog: 4 circuits, main circuit fsm
module fsm (
  input  in_1,
  input  [1:0] in_2,
  output out_3
);

  wire clock_1_out;
  wire [1:0] multiplexer_1_out, register_1_q, state3_0_1_state2;

  Clock clock_1 (.out(clock_1_out));
  // Probe on state3_0_1_state2
  state3_0 state3_0_1 (
    .before1(register_1_q[1]), .before2(register_1_q[0]), .input1(in_2[1]), .input2(in_2[0]),
    .state1(state3_0_1_state2[1]), .state2(state3_0_1_state2[0]));
  // Probe on register_1_q
  Multiplexer #(.width(2)) multiplexer_1 (
    .in0(state3_0_1_state2), .in1(2'b00), .out(multiplexer_1_out), .sel(in_1));  // open: en
  Register #(.width(2)) register_1 (.D(multiplexer_1_out), .Q(register_1_q), .clk(clock_1_out));  // open: en, clr
  out3_0 out3_0_1 (.s1(register_1_q[1]), .s2(register_1_q[0]), .i1(in_2[1]), .i2(in_2[0]), .out(out_3));
endmodule

module state2_0 (
  input  before1,
  input  before2,
  input  input1,
  input  input2,
  output state1,
  output state2
);

  wire and_1_out, and_2_out, and_3_out, and_4_out, and_5_out, not_1_out, not_2_out, not_3_out, not_4_out,
       not_5_out, not_6_out, not_7_out, not_8_out, not_9_out;

  not not_1 (not_1_out, before1);
  and and_1 (and_1_out, not_1_out, before2, not_2_out);
  not not_2 (not_2_out, input1);
  not not_3 (not_3_out, before1);
  and and_2 (and_2_out, not_3_out, before2, not_4_out);
  not not_4 (not_4_out, input2);
  not not_5 (not_5_out, before2);
  and and_3 (and_3_out, not_5_out, not_6_out, input2);
  not not_6 (not_6_out, input1);
  not not_7 (not_7_out, before1);
  and and_4 (and_4_out, not_7_out, before2, not_8_out);
  not not_8 (not_8_out, input2);
  not not_9 (not_9_out, input1);
  and and_5 (and_5_out, before1, not_9_out, input2);
  or or_1 (state1, and_1_out, and_2_out);
  or or_2 (state2, and_3_out, and_4_out, and_5_out);
endmodule

module out3_0 (
  input  s1,
  input  s2,
  input  i1,
  input  i2,
  output out
);

  wire not_1_out;

  and and_1 (out, s1, s2, not_1_out);
  not not_1 (not_1_out, i2);
endmodule

module state3_0 (
  input  before1,
  input  before2,
  input  input1,
  input  input2,
  output state1,
  output state2
);

  wire and_1_out, and_2_out, and_3_out, and_4_out, and_5_out, and_6_out, and_7_out, not_1_out, not_2_out,
       not_3_out, not_4_out, not_5_out, not_6_out, not_7_out, not_8_out, not_9_out, not_10_out, not_11_out,
       not_12_out, not_13_out;

  not not_1 (not_1_out, before1);
  and and_1 (and_1_out, not_1_out, before2, not_2_out);
  not not_2 (not_2_out, input1);
  not not_3 (not_3_out, before1);
  and and_2 (and_2_out, not_3_out, before2, not_4_out);
  not not_4 (not_4_out, input2);
  not not_5 (not_5_out, before2);
  and and_3 (and_3_out, before1, not_5_out, not_6_out);
  not not_6 (not_6_out, input2);
  not not_7 (not_7_out, before2);
  and and_4 (and_4_out, not_7_out, not_8_out, input2);
  not not_8 (not_8_out, input1);
  not not_9 (not_9_out, before1);
  and and_5 (and_5_out, not_9_out, before2, not_10_out);
  not not_10 (not_10_out, input2);
  and and_6 (and_6_out, before1, not_11_out, not_12_out);
  not not_11 (not_11_out, before2);
  not not_12 (not_12_out, input2);
  and and_7 (and_7_out, before1, not_13_out, input2);
  not not_13 (not_13_out, input1);
  or or_1 (state1, and_1_out, and_2_out, and_3_out);
  or or_2 (state2, and_4_out, and_5_out, and_6_out, and_7_out);
endmodule
