// Logisim project GRF.circ as structural Verilog: 6 circuits, main circuit grf
module grf (
  input  in_1,
  input  reset,
  input  WE,
  input  [4:0] A1,
  input  [4:0] A2,
  input  [4:0] A3,
  input  [31:0] WD,
  output [31:0] out_8,
  output [31:0] out_9
);

  wire or_1_out, or_2_out;
  wire [31:0] choose5_1_out_4, choose5_2_out_4;

  choose5 choose5_1 (.in_1({A3, in_1, reset, WE}), .in_2(A1), .in_3(WD), .out_4(choose5_1_out_4));
  choose5 choose5_2 (.in_1({A3, in_1, reset, WE}), .in_2(A2), .in_3(WD), .out_4(choose5_2_out_4));
  or or_1 (or_1_out, A1[0], A1[1], A1[2], A1[3], A1[4]);
  or or_2 (or_2_out, A2[0], A2[1], A2[2], A2[3], A2[4]);
  Multiplexer #(.width(32)) multiplexer_1 (
    .in0({32{1'b0}}), .in1(choose5_1_out_4), .out(out_8), .sel(or_1_out));  // open: en
  Multiplexer #(.width(32)) multiplexer_2 (
    .in0({32{1'b0}}), .in1(choose5_2_out_4), .out(out_9), .sel(or_2_out));  // open: en
endmodule

module choose1 (
  input  [3:0] write,
  input  read,
  input  [31:0] in_3,
  output [31:0] out_4
);

  wire [31:0] demultiplexer_1_out0, demultiplexer_1_out1, register_1_q, register_2_q;

  Demultiplexer #(.width(32), .tristate("true")) demultiplexer_1 (
    .out0(demultiplexer_1_out0), .out1(demultiplexer_1_out1), .in(in_3), .sel(write[3]));  // open: en
  Register #(.width(32)) register_1 (
    .D(demultiplexer_1_out0), .en(write[0]), .Q(register_1_q), .clk(write[2]), .clr(write[1]));
  Register #(.width(32)) register_2 (
    .D(demultiplexer_1_out1), .en(write[0]), .Q(register_2_q), .clk(write[2]), .clr(write[1]));
  Multiplexer #(.width(32)) multiplexer_1 (
    .in0(register_1_q), .in1(register_2_q), .out(out_4), .sel(read));  // open: en
endmodule

module choose2 (
  input  [4:0] write,
  input  [1:0] read,
  input  [31:0] in_3,
  output [31:0] out_4
);

  wire not_1_out;
  wire [0:0] and_1_out, and_2_out;
  wire [31:0] choose1_1_out_4, choose1_2_out_4, demultiplexer_1_out0, demultiplexer_1_out1;

  not not_1 (not_1_out, write[4]);
  and and_1 (and_1_out[0], not_1_out, write[0]);
  Demultiplexer #(.width(32)) demultiplexer_1 (
    .out0(demultiplexer_1_out0), .out1(demultiplexer_1_out1), .in(in_3), .sel(write[4]));  // open: en
  and and_2 (and_2_out[0], write[4], write[0]);
  choose1 choose1_1 (
    .write({write[3:1], and_1_out[0]}), .read(read[0]), .in_3(demultiplexer_1_out0), .out_4(choose1_1_out_4));
  choose1 choose1_2 (
    .write({write[3:1], and_2_out[0]}), .read(read[0]), .in_3(demultiplexer_1_out1), .out_4(choose1_2_out_4));
  Multiplexer #(.width(32)) multiplexer_1 (
    .in0(choose1_1_out_4), .in1(choose1_2_out_4), .out(out_4), .sel(read[1]));  // open: en
endmodule

module choose3 (
  input  [5:0] write,
  input  [2:0] read,
  input  [31:0] in_3,
  output [31:0] out_4
);

  wire not_1_out;
  wire [0:0] and_1_out, and_2_out;
  wire [31:0] choose2_1_out_4, choose2_2_out_4, demultiplexer_1_out0, demultiplexer_1_out1;

  not not_1 (not_1_out, write[5]);
  and and_1 (and_1_out[0], not_1_out, write[0]);
  Demultiplexer #(.width(32)) demultiplexer_1 (
    .out0(demultiplexer_1_out0), .out1(demultiplexer_1_out1), .in(in_3), .sel(write[5]));  // open: en
  and and_2 (and_2_out[0], write[5], write[0]);
  choose2 choose2_1 (
    .write({write[4:1], and_1_out[0]}), .read(read[1:0]), .in_3(demultiplexer_1_out0), .out_4(choose2_1_out_4));
  choose2 choose2_2 (
    .write({write[4:1], and_2_out[0]}), .read(read[1:0]), .in_3(demultiplexer_1_out1), .out_4(choose2_2_out_4));
  Multiplexer #(.width(32)) multiplexer_1 (
    .in0(choose2_1_out_4), .in1(choose2_2_out_4), .out(out_4), .sel(read[2]));  // open: en
endmodule

module choose4 (
  input  [6:0] in_1,
  input  [3:0] in_2,
  input  [31:0] in_3,
  output [31:0] out_4
);

  wire not_1_out;
  wire [0:0] and_1_out, and_2_out;
  wire [31:0] choose3_1_out_4, choose3_2_out_4, demultiplexer_1_out0, demultiplexer_1_out1;

  not not_1 (not_1_out, in_1[6]);
  and and_1 (and_1_out[0], in_1[6], in_1[0]);
  and and_2 (and_2_out[0], not_1_out, in_1[0]);
  Demultiplexer #(.width(32)) demultiplexer_1 (
    .out0(demultiplexer_1_out0), .out1(demultiplexer_1_out1), .in(in_3), .sel(in_1[6]));  // open: en
  // Probe on choose3_2_out_4
  // Probe on {in_1[5:1], and_1_out[0]}
  choose3 choose3_1 (
    .write({in_1[5:1], and_2_out[0]}), .read(in_2[2:0]), .in_3(demultiplexer_1_out0), .out_4(choose3_1_out_4));
  choose3 choose3_2 (
    .write({in_1[5:1], and_1_out[0]}), .read(in_2[2:0]), .in_3(demultiplexer_1_out1), .out_4(choose3_2_out_4));
  // Probe on choose3_1_out_4
  Multiplexer #(.width(32)) multiplexer_1 (
    .in0(choose3_1_out_4), .in1(choose3_2_out_4), .out(out_4), .sel(in_2[3]));  // open: en
endmodule

module choose5 (
  input  [7:0] in_1,
  input  [4:0] in_2,
  input  [31:0] in_3,
  output [31:0] out_4
);

  wire not_1_out;
  wire [0:0] and_1_out, and_2_out;
  wire [31:0] choose4_1_out_4, choose4_2_out_4, demultiplexer_1_out0, demultiplexer_1_out1;

  not not_1 (not_1_out, in_1[7]);
  and and_1 (and_1_out[0], in_1[0], in_1[7]);
  and and_2 (and_2_out[0], not_1_out, in_1[0]);
  Demultiplexer #(.width(32)) demultiplexer_1 (
    .out0(demultiplexer_1_out0), .out1(demultiplexer_1_out1), .in(in_3), .sel(in_1[7]));  // open: en
  choose4 choose4_1 (
    .in_1({in_1[6:1], and_2_out[0]}), .in_2(in_2[3:0]), .in_3(demultiplexer_1_out0), .out_4(choose4_1_out_4));
  choose4 choose4_2 (
    .in_1({in_1[6:1], and_1_out[0]}), .in_2(in_2[3:0]), .in_3(demultiplexer_1_out1), .out_4(choose4_2_out_4));
  Multiplexer #(.width(32)) multiplexer_1 (
    .in0(choose4_1_out_4), .in1(choose4_2_out_4), .out(out_4), .sel(in_2[4]));  // open: en
endmodule
