// Logisim project fbnq.circ as structural Verilog: 1 circuit, main circuit main
module main (
  input  [2:0] in_1,
  output [3:0] out_2
);

  wire clock_1_out, comparator_1_eq, comparator_1_gt, counter_1_q, not_1_out, or_1_out;
  wire [2:0] counter_2_q;
  wire [3:0] adder_1_out, multiplexer_1_out, register_1_q, register_2_q;

  Multiplexer #(.width(4)) multiplexer_1 (
    .in0(4'b0001), .in1(adder_1_out), .out(multiplexer_1_out), .sel(counter_1_q));  // open: en
  Counter #(.width(1), .max('h1), .ongoal("stay")) counter_1 (
    .Q(counter_1_q), .clk(clock_1_out));  // open: load, D, count, carry, clr
  Clock clock_1 (.out(clock_1_out));
  Counter #(.width(3), .max('h7)) counter_2 (
    .count(not_1_out), .Q(counter_2_q), .clk(clock_1_out));  // open: load, D, carry, clr
  Register #(.width(4)) register_1 (
    .D(multiplexer_1_out), .en(not_1_out), .Q(register_1_q), .clk(clock_1_out));  // open: clr
  Comparator #(.width(3), .mode("unsigned")) comparator_1 (
    .a(counter_2_q), .b(in_1), .gt(comparator_1_gt), .eq(comparator_1_eq));  // open: lt
  not not_1 (not_1_out, or_1_out);
  Register #(.width(4)) register_2 (.D(register_1_q), .Q(register_2_q), .clk(clock_1_out));  // open: en, clr
  or or_1 (or_1_out, comparator_1_gt, comparator_1_eq);
  Adder #(.width(4)) adder_1 (.a(register_1_q), .b(register_2_q), .out(adder_1_out));  // open: cin, cout
  Multiplexer #(.width(4)) multiplexer_2 (.in0(4'b0000), .in1(register_1_q), .out(out_2), .sel(or_1_out));  // open: en
endmodule
