// Logisim project 2n_mol5.circ as structural Verilog: 3 circuits, main circuit mod5
module mod5 (
  input  in_1,
  output out_2,
  output out_3,
  output out_4,
  output out_5,
  output out_6
);

  wire clock_1_out;
  wire [1:1] register_1_q;

  Clock clock_1 (.out(clock_1_out));
  Register #(.width(1)) register_1 (.D(in_1), .Q(register_1_q[1]), .clk(clock_1_out));  // open: en, clr
  Demultiplexer #(.select(2)) demultiplexer_1 (
    .out0(out_3), .out1(out_4), .out2(out_6), .out3(out_5), .in(1'b1), .sel({register_1_q[1], in_1}),
    .en(1'b1));

  assign out_2 = 1'b0;
endmodule

module D (
  input  in_1,
  input  in_2,
  output out_3,
  output out_4
);

  wire and_1_out, and_2_out, not_1_out;

  not not_1 (not_1_out, in_2);
  and and_1 (and_1_out, in_1, not_1_out);
  and and_2 (and_2_out, in_1, in_2);
  nor nor_1 (out_3, and_1_out, out_4);
  nor nor_2 (out_4, out_3, and_2_out);
endmodule

module D_2_0 (
  input  in_1,
  input  in_2,
  output out_3
);

  wire d_1_out_3, not_1_out;

  not not_1 (not_1_out, in_1);
  D d_1 (.in_1(not_1_out), .in_2(in_2), .out_3(d_1_out_3));  // open: out_4
  D d_2 (.in_1(in_1), .in_2(d_1_out_3), .out_3(out_3));  // open: out_4
endmodule
