// Logisim project add.circ as structural Verilog: 1 circuit, main circuit main
module main (
  input  [2:0] in_1,
  output [3:0] out_2
);

  wire clock_1_out, counter_1_q;
  wire [3:0] multiplexer_1_out, register_1_q, register_2_q;

  Clock clock_1 (.out(clock_1_out));
  Counter #(.width(1), .max('h1), .ongoal("stay")) counter_1 (
    .Q(counter_1_q), .clk(clock_1_out));  // open: load, D, count, carry, clr
  Multiplexer #(.width(4)) multiplexer_1 (
    .in0(4'b0001), .in1(out_2), .out(multiplexer_1_out), .sel(counter_1_q));  // open: en
  Register #(.width(4)) register_1 (.D(multiplexer_1_out), .Q(register_1_q), .clk(clock_1_out));  // open: en, clr
  // Probe on multiplexer_1_out
  Register #(.width(4)) register_2 (.Q(register_2_q), .clk(clock_1_out));  // open: D, en, clr
  Adder #(.width(4)) adder_1 (.a(register_1_q), .b(register_2_q), .out(out_2));  // open: cin, cout
endmodule
