// Logisim project swap.circ as structural Verilog: 2 circuits, main circuit swap
module swap (
  input  I1,
  input  I1_2,
  input  S,
  output O1,
  output O2
);

  wire and_1_out, and_2_out, or_1_out, or_2_out, xor_1_out, xor_2_out;

  or or_1 (or_1_out, S, I1);
  and and_1 (and_1_out, S, I1);
  and and_2 (and_2_out, S, I1_2);
  or or_2 (or_2_out, S, I1_2);
  xor xor_1 (xor_1_out, S, or_1_out);
  xor xor_2 (xor_2_out, or_2_out, S);
  or or_3 (O1, xor_1_out, and_2_out);
  or or_4 (O2, xor_2_out, and_1_out);
endmodule

module test2 (
  input  a,
  input  b,
  input  s,
  output c,
  output d
);

  wire and_1_out, and_2_out, and_3_out, and_4_out, not_1_out, not_2_out;

  not not_1 (not_1_out, s);
  not not_2 (not_2_out, s);
  and and_1 (and_1_out, b, s);
  and and_2 (and_2_out, a, not_1_out);
  and and_3 (and_3_out, b, not_2_out);
  and and_4 (and_4_out, a, s);
  or or_1 (c, and_1_out, and_2_out);
  or or_2 (d, and_3_out, and_4_out);
endmodule
