// Logisim project navigation.circ as structural Verilog: 3 circuits, main circuit navigation
module navigation (
  input  [1:0] in_1,
  input  in_2,
  input  r,
  output arrive,
  output hit
);

  wire comparator_2_eq;
  wire [2:0] register_1_q, state2_0_1_s3;

  state2_0 state2_0_1 (
    .b1(register_1_q[2]), .b2(register_1_q[1]), .b3(register_1_q[0]), .i1(in_1[1]), .i2(in_1[0]),
    .s1(state2_0_1_s3[2]), .s2(state2_0_1_s3[1]), .s3(state2_0_1_s3[0]));
  Register #(.width(3)) register_1 (.D(state2_0_1_s3), .Q(register_1_q), .clk(in_2), .clr(r));  // open: en
  Comparator #(.width(3)) comparator_1 (.a(3'b100), .b(register_1_q), .eq(arrive));  // open: gt, lt
  Comparator #(.width(3)) comparator_2 (.a(register_1_q), .b(state2_0_1_s3), .eq(comparator_2_eq));  // open: gt, lt
  Register #(.width(1)) register_2 (.D(comparator_2_eq), .Q(hit), .clk(in_2), .clr(r));  // open: en
endmodule

module state (
  input  b1,
  input  b2,
  input  b3,
  input  i1,
  input  i2,
  output s1,
  output s2,
  output s3
);

  wire and_1_out, and_2_out, and_3_out, and_4_out, and_5_out, and_6_out, and_7_out, and_8_out, and_9_out,
       and_10_out, and_11_out, and_12_out, not_1_out, not_2_out, not_3_out, not_4_out, not_5_out, not_6_out,
       not_7_out, not_8_out, not_9_out, not_10_out, not_11_out, not_12_out, not_13_out, not_14_out,
       not_15_out, not_16_out, not_17_out, not_18_out, not_19_out, not_20_out, not_21_out, not_22_out,
       not_23_out, not_24_out, not_25_out, not_26_out, not_27_out, not_28_out, not_29_out;

  not not_1 (not_1_out, b1);
  not not_2 (not_2_out, b3);
  not not_3 (not_3_out, i1);
  not not_4 (not_4_out, i2);
  not not_5 (not_5_out, b1);
  not not_6 (not_6_out, i1);
  not not_7 (not_7_out, b2);
  not not_8 (not_8_out, b3);
  not not_9 (not_9_out, b1);
  not not_10 (not_10_out, b2);
  not not_11 (not_11_out, i1);
  not not_12 (not_12_out, b1);
  not not_13 (not_13_out, i1);
  not not_14 (not_14_out, i2);
  not not_15 (not_15_out, b1);
  not not_16 (not_16_out, b3);
  not not_17 (not_17_out, i1);
  not not_18 (not_18_out, b1);
  not not_19 (not_19_out, b3);
  not not_20 (not_20_out, i2);
  not not_21 (not_21_out, b1);
  not not_22 (not_22_out, b1);
  not not_23 (not_23_out, b2);
  not not_24 (not_24_out, i1);
  not not_25 (not_25_out, i2);
  not not_26 (not_26_out, b1);
  not not_27 (not_27_out, b1);
  not not_28 (not_28_out, b1);
  not not_29 (not_29_out, i2);
  and and_1 (and_1_out, not_1_out, b2, not_2_out, not_3_out, not_4_out);
  and and_2 (and_2_out, not_5_out, b2, b3, not_6_out, i2);
  and and_3 (and_3_out, b1, not_7_out, not_8_out);
  and and_4 (and_4_out, not_9_out, not_10_out, b3, not_11_out);
  and and_5 (and_5_out, not_12_out, b3, not_13_out, not_14_out);
  and and_6 (and_6_out, not_15_out, b2, not_16_out, not_17_out, i2);
  and and_7 (and_7_out, not_18_out, b2, not_19_out, i1, not_20_out);
  and and_8 (and_8_out, not_21_out, b2, b3, i1, i2);
  and and_9 (and_9_out, not_22_out, not_23_out, not_24_out, not_25_out);
  and and_10 (and_10_out, not_26_out, b3, i1, i2);
  and and_11 (and_11_out, not_27_out, b2, i1, i2);
  and and_12 (and_12_out, not_28_out, b2, b3, not_29_out);
  or or_1 (s1, and_1_out, and_2_out, and_3_out);
  or or_2 (s2, and_4_out, and_5_out, and_6_out, and_7_out, and_8_out);
  or or_3 (s3, and_9_out, and_10_out, and_11_out, and_12_out);
endmodule

module state2_0 (
  input  b1,
  input  b2,
  input  b3,
  input  i1,
  input  i2,
  output s1,
  output s2,
  output s3
);

  wire and_1_out, and_2_out, and_3_out, and_4_out, and_5_out, and_6_out, and_7_out, and_8_out, and_9_out,
       and_10_out, and_11_out, not_1_out, not_2_out, not_3_out, not_4_out, not_5_out, not_6_out, not_7_out,
       not_8_out, not_9_out, not_10_out, not_11_out, not_12_out, not_13_out, not_14_out, not_15_out,
       not_16_out, not_17_out, not_18_out, not_19_out, not_20_out, not_21_out, not_22_out, not_23_out,
       not_24_out, not_25_out, not_26_out, not_27_out;

  not not_1 (not_1_out, b1);
  not not_2 (not_2_out, b3);
  not not_3 (not_3_out, i1);
  not not_4 (not_4_out, i2);
  not not_5 (not_5_out, b1);
  not not_6 (not_6_out, i1);
  not not_7 (not_7_out, b1);
  not not_8 (not_8_out, b2);
  not not_9 (not_9_out, i1);
  not not_10 (not_10_out, b1);
  not not_11 (not_11_out, i1);
  not not_12 (not_12_out, i2);
  not not_13 (not_13_out, b1);
  not not_14 (not_14_out, b3);
  not not_15 (not_15_out, i1);
  not not_16 (not_16_out, b1);
  not not_17 (not_17_out, b3);
  not not_18 (not_18_out, i2);
  not not_19 (not_19_out, b1);
  not not_20 (not_20_out, b1);
  not not_21 (not_21_out, b2);
  not not_22 (not_22_out, i1);
  not not_23 (not_23_out, i2);
  not not_24 (not_24_out, b1);
  not not_25 (not_25_out, b1);
  not not_26 (not_26_out, b1);
  not not_27 (not_27_out, i2);
  and and_1 (and_1_out, not_1_out, b2, not_2_out, not_3_out, not_4_out);
  and and_2 (and_2_out, not_5_out, b2, b3, not_6_out, i2);
  and and_3 (and_3_out, not_7_out, not_8_out, b3, not_9_out);
  and and_4 (and_4_out, not_10_out, b3, not_11_out, not_12_out);
  and and_5 (and_5_out, not_13_out, b2, not_14_out, not_15_out, i2);
  and and_6 (and_6_out, not_16_out, b2, not_17_out, i1, not_18_out);
  and and_7 (and_7_out, not_19_out, b2, b3, i1, i2);
  and and_8 (and_8_out, not_20_out, not_21_out, not_22_out, not_23_out);
  and and_9 (and_9_out, not_24_out, b3, i1, i2);
  and and_10 (and_10_out, not_25_out, b2, i1, i2);
  and and_11 (and_11_out, not_26_out, b2, b3, not_27_out);
  or or_1 (s1, and_1_out, and_2_out);
  or or_2 (s2, and_3_out, and_4_out, and_5_out, and_6_out, and_7_out);
  or or_3 (s3, and_8_out, and_9_out, and_10_out, and_11_out);
endmodule
